# Fritzing sketch cloning (saved by Fritzing 0.9.3b)
breadboards: 1

parts:
  U1 = ESP32S-HiLetgo [part_number=ESP32S-HiLetgo]
  S1 = Pushbutton [package="[SMD]"]
  R1 = Resistor [tolerance=±5% resistance=220 package=THT]
  Grove1 = Grove Infrared Receiver
  J1 = Piezo Speaker

nets:
  N1: U1.3.3, R1.Pin_0, Grove1.VCC
  GND: U1.GND, S1.Pin_1, S1.Pin_2, Grove1.GND, J1.pin1
  N2: U1.GPIO18, S1.Pin_3, S1.Pin_4, R1.Pin_1
  N3: U1.GPIO19, Grove1.RX

custom parts:
  ESP32S-HiLetgo: HiLetgo ESP-WROOM-32 ESP32 ESP-32S Development Board 2.4GHz Dual-Mode WiFi + Bluetooth Dual Cores Microcontroller The ESP32 integrated with Antenna switches, RF Balun, power amplifiers, low-noise amplifiers, filters, and management modules, and the entire solution occupies the least area of PCB. 2.4 GHz Wi-Fi plus Bluetooth dual-mode chip, with TSMC Ultra-low power consumption 40nm technology,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
